// Digital circuit ALU_Integração.dig as structural Verilog
module \ALU_Integração  (
  input  [2:0] OP,
  input  [7:0] A,
  input  [7:0] B,
  input  CLOCK,
  input  LOAD,
  output [7:0] OUT
);

  wire somador_subtrator_8bits_1_cout, somador_subtrator_8bits_2_cout;
  wire [7:0] DATA, R_ADD, R_DIV_q, R_DIV_r, R_MULT_High, R_MULT_Low, R_NAND, R_SHL, R_SHR, R_SUB, R_XOR;

  somador_subtrator_8bits somador_subtrator_8bits_1 (
    .A(A), .B(B), .SUB(1'b0), .COUT(somador_subtrator_8bits_1_cout), .S(R_ADD));
  somador_subtrator_8bits somador_subtrator_8bits_2 (
    .A(A), .B(B), .SUB(1'b1), .COUT(somador_subtrator_8bits_2_cout), .S(R_SUB));
  // XOR xor_1: pin names not known; wires that end beside it: A, B, R_XOR
  // NAND nand_1: pin names not known; wires that end beside it: A, B, R_NAND
  Shift_Left shift_left_1 (.AC(OUT), .S(R_SHL));
  Shift_Right shift_right_1 (.AC(OUT), .S(R_SHR));
  Mul #(.Bits(8)) mul_1 (.a(A), .b(B), .mul({R_MULT_High, R_MULT_Low}));
  Div #(.Bits(8)) div_1 (.a(A), .b(B), .q(R_DIV_q), .r(R_DIV_r));
  LED OVERFLOW (.in(somador_subtrator_8bits_1_cout));
  LED OVERFLOW_2 (.in(somador_subtrator_8bits_2_cout));
  Seletor seletor_1 (
    .R_ADD(R_ADD), .R_SUB(R_SUB), .R_XOR(R_XOR), .R_NAND(R_NAND), .R_SHL(R_SHL), .R_SHR(R_SHR),
    .R_MULT(R_MULT_Low), .R_DIV(R_DIV_q), .OP(OP), .S(DATA));
  REG_AC_8Bit reg_ac_8bit_1 (.DATA(DATA), .STORE_AC(LOAD), .CLOCK(CLOCK), .D(OUT));

  // Other names for the same wires on the sheet: AC[7:0] = OUT

  // Notes on the sheet:
  //   OP0 - Adição
  //   OP1 - Subtração
  //   OP2 - XOR
  //   OP3 - NAND
  //   OP4 - Shift Left
  //   OP5 - Shift Right
  //   OP6 - Multiplicação
  //   OP7 - Divisão
  //   ALU - Integração
  //   Aqui estaremos integrando todos os módulos criados
endmodule
