// Digital circuit CPU - Ring counter + tri-state bus.dig as structural Verilog
module CPU___Ring_counter___tri_state_bus (
  input  EN,
  input  clr,
  input  L_M,
  input  E_P,
  input  E_R,
  output [3:0] DEBUG_MAR,
  output [3:0] DEBUG_MAR_Q,
  output [3:0] DEBUG_BUS_LOW,
  output [3:0] DEBUG_BUS_HIGH,
  output [3:0] DEBUG_BUS_LOW_2,
  output [3:0] DEBUG_PC
);

  wire BUS, CLK, counter_1_ovf, T1, T2, T3, T4, T5, T6;
  wire [3:0] eeprom_1_d;

  Button CLOCK (.out(CLK));
  Counter #(.Bits(4)) counter_1 (.en(EN), .C(T2), .clr(clr), .out(DEBUG_PC), .ovf(counter_1_ovf));
  Register #(.Bits(4)) register_1 (.D(DEBUG_BUS_LOW), .C(CLK), .en(~L_M), .Q(DEBUG_MAR));
  Multiplexer #(.Bits(4)) multiplexer_1 (.sel(1'b1), .in_0(4'b0000), .in_1(DEBUG_MAR), .out(DEBUG_MAR_Q));
  ring_counter ring_counter_1 (.CLK(CLK), .T1(T1), .T2(T2), .T3(T3), .T4(T4), .T5(T5), .T6(T6));
  LED led_1 (.in(counter_1_ovf));
  EEPROM #(.AddrBits(4), .Bits(4)) eeprom_1 (.A(DEBUG_MAR_Q), .CS(1'b1), .WE(1'b0), .OE(1'b1), .D(eeprom_1_d));
  EEPROM #(.AddrBits(4), .Bits(4)) eeprom_2 (.A(DEBUG_MAR_Q), .CS(1'b1), .WE(1'b0), .OE(1'b1), .D(DEBUG_BUS_HIGH));
  assign DEBUG_BUS_LOW = E_P ? DEBUG_PC : 4'bz;  // Driver driver_1
  assign DEBUG_BUS_LOW = E_R ? eeprom_1_d : 4'bz;  // Driver driver_2
  // NotConnected on BUS

  assign DEBUG_BUS_LOW_2 = DEBUG_BUS_LOW;

  // Other names for the same wires on the sheet: BUS_HIGH[3:0] = DEBUG_BUS_HIGH; BUS_LOW[3:0] = DEBUG_BUS_LOW;
  //   MAR_Q[3:0] = DEBUG_MAR_Q; nL_M = L_M; Q[3:0] = DEBUG_MAR

  // Notes on the sheet:
  //   CPU - Ring counter + tri-state bus
  //   Aqui estaremos integrando todos os módulos criados 
  //   para a produção da CPU
  //   Ring Counter
  //   PC (Program Counter)
  //   (Program Counter)
  //   0 - READ
  //   1 - WRITE
  //   Ver  155 Malvino
  //   RING COUNTER
  //   PC
  //   MAR
  //   0 - PROG
  //   1 - RUN
  //   Ver  153 Malvino
  //   RAM 16x2
  //   RANDOM ACCESS MEMORY
  //   contents of eeprom_1 (hex, n*v repeats v):
  //   8,211,11,a,3
  //   contents of eeprom_2 (hex, n*v repeats v):
  //   13,9c,0,153,13,13
endmodule
