// Digital circuit NAND.dig as structural Verilog
module NAND (
  input  [7:0] AC,
  input  [7:0] N,
  output [7:0] S
);

  wire [7:0] and_1_out;

  assign and_1_out = AC & N;  // And and_1, 8 bits wide
  assign S = ~and_1_out;  // Not not_1, 8 bits wide

  // Notes on the sheet:
  //   NAND
endmodule
