// Digital circuit XOR.dig as structural Verilog
module XOR (
  input  [7:0] N,
  input  [7:0] AC,
  output [7:0] S
);

  assign S = N ^ AC;  // XOr xor_1, 8 bits wide

  // Notes on the sheet:
  //   XOR
endmodule
