// Digital circuit ring_counter.dig as structural Verilog
module ring_counter (
  input  CLK,
  output T1,
  output T2,
  output T3,
  output T4
);

  D_FF d_ff_1 (.D(T4), .C(CLK), .Q(T1));  // open: nQ
  D_FF d_ff_2 (.D(T1), .C(CLK), .Q(T2));  // open: nQ
  D_FF d_ff_3 (.D(T2), .C(CLK), .Q(T3));  // open: nQ
  D_FF #(.Default(1)) d_ff_4 (.D(T3), .C(CLK), .Q(T4));  // open: nQ

  // Notes on the sheet:
  //   Ring Counter
  //   4 FlipFlop tipo D. O Primeiro está setado com padrão 1
endmodule
